# Fritzing sketch AxoControllerV2 (saved by Fritzing 0.9.3b)
breadboards: 1

parts:
  WeMos_D1_Mini1 = WeMos D1 Mini  # not connected
  IC2 = IC, DIP package, 8 pins [chip_label=MAX604 part_number=MAX604]
  J1 = male pin header, 4 pins [form="♂ (male)"]
  R1 = Resistor [tolerance=±5% resistance=4.7k package=THT]
  J2 = male pin header, 3 pins [form="♂ (male)"]
  Power_plug1 = Power plug

nets:
  N1: IC2.pin1, IC2.pin4, J1.pin3, Power_plug1.VCC
  N2: IC2.pin2, IC2.pin5, IC2.pin6, J1.pin4, J2.pin3, Power_plug1.GND
  N3: IC2.pin8, R1.Pin_1, J2.pin1
  N4: R1.Pin_0, J2.pin2

notes:
  3V3
  12V
  Cnt
  Sens
