# Fritzing sketch AxoQController (saved by Fritzing 0.9.3b)
breadboards: 1

parts:
  IC1 = IC, DIP package, 8 pins [chip_label=MAX604 part_number=MAX604]
  Adafruit_HUZZAH_ESP8266_Breakout1 = Adafruit HUZZAH ESP8266 Breakout [part_number=2471]
  Power_plug1 = Power plug
  R1 = Resistor [tolerance=±5% resistance=4.7k package=THT]
  Q1 = NPN-Transistor [part_number=2SD467 package="TO92 [THT]"]
  R2 = Resistor [tolerance=±5% resistance=1k package=THT]
  J1 = Screw terminal - 2 pins [part_number="12V Fan" package=THT]
  DS1 = DS18B20 1-Wire Temperature Sensor [part_number=DS18B20]
  D1 = Rectifier Diode [part_number=1N4001 package="300 mil [THT]"]

nets:
  12V: IC1.pin1, IC1.pin4, Power_plug1.VCC, J1.pin1, D1.cathode
  GND: IC1.pin2, IC1.pin5, IC1.pin6, IC1.pin7, Adafruit_HUZZAH_ESP8266_Breakout1.GND, Power_plug1.GND, Q1.E, DS1.GND
  5V: IC1.pin8, Adafruit_HUZZAH_ESP8266_Breakout1.VBat
  N1: Adafruit_HUZZAH_ESP8266_Breakout1.#13, R2.Pin_0
  N2: Adafruit_HUZZAH_ESP8266_Breakout1.#2, R1.Pin_0, DS1.DQ
  N3: Adafruit_HUZZAH_ESP8266_Breakout1.3V, R1.Pin_1, DS1.VDD
  N4: Q1.B, R2.Pin_1
  N5: Q1.C, J1.pin2, D1.anode
